// Logisim project homework1.circ as structural Verilog: 1 circuit, main circuit main
module main (
  input  in_1,
  input  in_2,
  input  in_3,
  output out_4,
  output out_5,
  output out_6,
  output out_7
);

  wire and_1_out, and_2_out, and_3_out, and_4_out, and_5_out, not_1_out, not_2_out, not_3_out, not_4_out,
       not_5_out, not_6_out, not_7_out, or_1_out, or_2_out, or_3_out, or_4_out;

  not not_1 (not_1_out, in_1);
  not not_2 (not_2_out, in_3);
  not not_3 (not_3_out, in_1);
  not not_4 (not_4_out, in_3);
  not not_5 (not_5_out, in_1);
  not not_6 (not_6_out, in_3);
  and and_1 (and_1_out, in_2, in_3);
  not not_7 (not_7_out, in_3);
  or or_1 (or_1_out, in_1, in_3);
  or or_2 (or_2_out, not_3_out, in_2, not_4_out);
  or or_3 (or_3_out, in_1, in_2);
  or or_4 (or_4_out, not_5_out, not_6_out);
  and and_2 (and_2_out, not_7_out, in_1);
  and and_3 (and_3_out, in_2, in_1);
  and and_4 (and_4_out, not_1_out, in_3);
  and and_5 (and_5_out, in_1, not_2_out);
  and and_6 (out_6, or_1_out, or_2_out);
  and and_7 (out_7, or_3_out, or_4_out);
  or or_5 (out_4, and_1_out, and_2_out);
  or or_6 (out_5, and_3_out, and_4_out, and_5_out);

  // Other names for the same wires on the sheet: x1 = in_1; x2 = in_2; x3 = in_3
endmodule
